# Fritzing sketch frizing 회로도 (saved by Fritzing 0.9.2b)
breadboards: 1

parts:
  GY1 = GY-521 (MPU-6050) [form="♀ (female)" package=THT]  # not connected
  부품1 = Arduino Leonardo (Rev3b)
  S1 = Pushbutton [package="[THT]"]
  S2 = Pushbutton [package="[THT]"]
  S3 = Pushbutton [package="[THT]"]
  U1 = POT [package=pot_alpha_rv16af-20]
  R1 = Resistor [tolerance=±5% resistance=10 package=THT]
  R2 = Resistor [tolerance=±5% resistance=10 package=THT]  # not connected
  R3 = Resistor [tolerance=±5% resistance=10 package=THT]

nets:
  N1: 부품1.GND, U1.E
  N2: 부품1.A0, U1.S
  N3: 부품1.D11_PWM, S1.Pin_1, S1.Pin_2
  N4: 부품1.D12/A11, S2.Pin_1, S2.Pin_2, R3.Pin_0
  N5: 부품1.D13_PWM, S3.Pin_1, S3.Pin_2, R1.Pin_0
  N6: S1.Pin_3, S1.Pin_4, S2.Pin_3, S2.Pin_4, S3.Pin_3, S3.Pin_4
  N7: R1.Pin_1, R3.Pin_1

custom parts:
  GY-521 (MPU-6050): Placa GY-521 basada en conjunto de acelerómetro+giroscopios MPU-6050
